// Logisim project task1.circ as structural Verilog: 2 circuits, main circuit main
module main (
  input  in_1,
  input  in_2,
  input  in_3,
  input  in_4,
  input  in_5,
  input  in_6,
  input  in_7,
  input  in_8,
  input  in_9,
  input  in_10,
  input  in_11,
  input  in_12,
  input  in_13,
  input  in_14,
  input  in_15,
  input  in_16,
  output out_17,
  output out_18,
  output out_19,
  output out_20,
  output out_21,
  output out_22,
  output out_23,
  output out_24,
  output Error
);

  wire subtractor_1_nborrow, subtractor_2_nborrow, subtractor_3_nborrow, subtractor_4_nborrow,
       subtractor_5_nborrow, subtractor_6_nborrow, subtractor_7_nborrow;

  subtractor subtractor_1 (.a(in_8), .b(in_16), .borrow(1'b0), .c(out_24), .nborrow(subtractor_1_nborrow));
  subtractor subtractor_2 (
    .a(in_7), .b(in_15), .borrow(subtractor_1_nborrow), .c(out_23), .nborrow(subtractor_2_nborrow));
  subtractor subtractor_3 (
    .a(in_6), .b(in_14), .borrow(subtractor_2_nborrow), .c(out_22), .nborrow(subtractor_3_nborrow));
  subtractor subtractor_4 (
    .a(in_5), .b(in_13), .borrow(subtractor_3_nborrow), .c(out_21), .nborrow(subtractor_4_nborrow));
  subtractor subtractor_5 (
    .a(in_4), .b(in_12), .borrow(subtractor_4_nborrow), .c(out_20), .nborrow(subtractor_5_nborrow));
  subtractor subtractor_6 (
    .a(in_3), .b(in_11), .borrow(subtractor_5_nborrow), .c(out_19), .nborrow(subtractor_6_nborrow));
  subtractor subtractor_7 (
    .a(in_2), .b(in_10), .borrow(subtractor_6_nborrow), .c(out_18), .nborrow(subtractor_7_nborrow));
  subtractor subtractor_8 (.a(in_1), .b(in_9), .borrow(subtractor_7_nborrow), .c(out_17), .nborrow(Error));
endmodule

module subtractor (
  input  a,
  input  b,
  input  borrow,
  output c,
  output nborrow
);

  wire and_1_out, and_2_out, and_3_out, not_1_out, not_2_out, not_3_out, or_1_out, or_2_out, or_3_out,
       or_4_out, or_5_out, or_6_out, or_7_out, or_8_out, or_9_out, or_10_out, or_11_out;

  not not_1 (not_1_out, a);
  not not_2 (not_2_out, b);
  not not_3 (not_3_out, borrow);
  or or_1 (or_1_out, a, b);
  or or_2 (or_2_out, a, not_2_out);
  or or_3 (or_3_out, not_1_out, b);
  or or_4 (or_4_out, not_1_out, not_2_out);
  or or_5 (or_5_out, b, borrow);
  or or_6 (or_6_out, not_1_out, b);
  or or_7 (or_7_out, or_1_out, borrow);
  or or_8 (or_8_out, or_2_out, not_3_out);
  or or_9 (or_9_out, or_3_out, not_3_out);
  or or_10 (or_10_out, or_4_out, borrow);
  and and_1 (and_1_out, or_5_out, or_6_out);
  or or_11 (or_11_out, not_1_out, borrow);
  and and_2 (and_2_out, or_7_out, or_8_out);
  and and_3 (and_3_out, or_9_out, or_10_out);
  and and_4 (nborrow, and_1_out, or_11_out);
  and and_5 (c, and_2_out, and_3_out);
endmodule
