// Logisim project task2.circ as structural Verilog: 5 circuits, main circuit main
module main (
  input  in_1,
  input  in_2,
  input  in_3,
  input  in_4,
  input  in_5,
  input  in_6,
  input  in_7,
  input  in_8,
  output out_9,
  output out_10,
  output out_11,
  output out_12,
  output out_13,
  output out_14,
  output out_15,
  output out_16,
  output out_17,
  output out_18,
  output out_19,
  output out_20,
  output out_21
);

  wire add6in8421bcd_1_carry;

  add8421bcd add8421bcd_1 (
    .A1(in_1), .A2(in_2), .A3(in_3), .A4(in_4), .B1(in_5), .B2(in_6), .B3(in_7), .B4(in_8), .Carry(1'b0),
    .C1(out_18), .C2(out_19), .C3(out_20), .C4(out_21), .NCarry(out_17));
  add6in8421bcd add6in8421bcd_1 (
    .A1(out_18), .A2(out_19), .A3(out_20), .A4(out_21), .B1(out_13), .B2(out_14), .B3(out_15), .B4(out_16),
    .Carry(add6in8421bcd_1_carry));
  add8421bcd add8421bcd_2 (
    .A1(1'b0), .A2(1'b0), .A3(1'b0), .A4(add6in8421bcd_1_carry), .B1(1'b0), .B2(1'b0), .B3(1'b0),
    .B4(out_17), .Carry(1'b0), .C1(out_9), .C2(out_10), .C3(out_11), .C4(out_12));  // open: NCarry
endmodule

module add8421bcd (
  input  A1,
  input  A2,
  input  A3,
  input  A4,
  input  B1,
  input  B2,
  input  B3,
  input  B4,
  input  Carry,
  output C1,
  output C2,
  output C3,
  output C4,
  output NCarry
);

  wire add_1_ncarry, add_2_c, add_2_ncarry, add_3_c, add_3_ncarry, add_4_c, add_4_ncarry, add_5_ncarry,
       add_6_ncarry, add_7_ncarry, is_invalid_1_out_5, or_1_out;

  add add_1 (.A(A4), .B(B4), .Carry(Carry), .C(C4), .NCarry(add_1_ncarry));
  add add_2 (.A(A3), .B(B3), .Carry(add_1_ncarry), .C(add_2_c), .NCarry(add_2_ncarry));
  add add_3 (.A(A2), .B(B2), .Carry(add_2_ncarry), .C(add_3_c), .NCarry(add_3_ncarry));
  add add_4 (.A(A1), .B(B1), .Carry(add_3_ncarry), .C(add_4_c), .NCarry(add_4_ncarry));
  is_invalid is_invalid_1 (.A1(add_4_c), .A2(add_3_c), .A3(add_2_c), .A4(C4), .out_5(is_invalid_1_out_5));
  or or_1 (or_1_out, is_invalid_1_out_5, add_4_ncarry);
  add add_5 (.A(add_2_c), .B(or_1_out), .Carry(1'b0), .C(C3), .NCarry(add_5_ncarry));
  add add_6 (.A(add_3_c), .B(or_1_out), .Carry(add_5_ncarry), .C(C2), .NCarry(add_6_ncarry));
  add add_7 (.A(add_4_c), .B(add_6_ncarry), .Carry(1'b0), .C(C1), .NCarry(add_7_ncarry));
  or or_2 (NCarry, add_7_ncarry, add_4_ncarry);
endmodule

module add (
  input  A,
  input  B,
  input  Carry,
  output C,
  output NCarry
);

  wire and_1_out, and_2_out, and_3_out, and_4_out, and_5_out, and_6_out, and_7_out, not_1_out, not_2_out,
       not_3_out, not_4_out, or_1_out, or_2_out;

  not not_1 (not_1_out, A);
  not not_2 (not_2_out, B);
  and and_1 (and_1_out, A, B);
  and and_2 (and_2_out, A, Carry);
  and and_3 (and_3_out, Carry, B);
  and and_4 (and_4_out, not_1_out, B);
  and and_5 (and_5_out, not_2_out, A);
  or or_1 (or_1_out, and_4_out, and_5_out);
  or or_2 (or_2_out, and_1_out, and_2_out);
  not not_3 (not_3_out, Carry);
  not not_4 (not_4_out, or_1_out);
  or or_3 (NCarry, or_2_out, and_3_out);
  and and_6 (and_6_out, not_3_out, or_1_out);
  and and_7 (and_7_out, not_4_out, Carry);
  or or_4 (C, and_6_out, and_7_out);
endmodule

module is_invalid (
  input  A1,
  input  A2,
  input  A3,
  input  A4,
  output out_5
);

  wire or_1_out;

  or or_1 (or_1_out, A2, A3);
  and and_1 (out_5, A1, or_1_out);
endmodule

module add6in8421bcd (
  input  A1,
  input  A2,
  input  A3,
  input  A4,
  output B1,
  output B2,
  output B3,
  output B4,
  output Carry
);

  add8421bcd add8421bcd_1 (
    .A1(A1), .A2(A2), .A3(A3), .A4(A4), .B1(1'b0), .B2(1'b1), .B3(1'b1), .B4(1'b0), .Carry(1'b0), .C1(B1),
    .C2(B2), .C3(B3), .C4(B4), .NCarry(Carry));
endmodule
