// Logisim project task3.circ as structural Verilog: 1 circuit, main circuit main
module main (
);

  wire clock_1_out, nand_1_out, nand_2_out, t_ff_1_qn, t_ff_2_q, t_ff_2_qn, t_ff_3_q, t_ff_3_qn;

  T_Flip_Flop t_ff_1 (.T(1'b1), .clk(nand_1_out), .Qn(t_ff_1_qn));  // open: Q, reset, preset
  LED led_1 (.in(t_ff_1_qn));
  T_Flip_Flop t_ff_2 (.T(1'b1), .clk(nand_2_out), .Q(t_ff_2_q), .Qn(t_ff_2_qn));  // open: reset, preset
  LED led_2 (.in(t_ff_2_qn));
  Clock clock_1 (.out(clock_1_out));
  nand nand_1 (nand_1_out, t_ff_2_q, t_ff_2_q);
  T_Flip_Flop t_ff_3 (.T(1'b1), .clk(clock_1_out), .Q(t_ff_3_q), .Qn(t_ff_3_qn));  // open: reset, preset
  LED led_3 (.in(t_ff_3_qn));
  nand nand_2 (nand_2_out, t_ff_3_q, t_ff_3_q);
endmodule
